# Fritzing sketch Dispensador (saved by Fritzing 0.9.3b)
circuit board: 10.1421cm x 5.31149cm
breadboards: 1

parts:
  Componente1 = Arduino Mega 2560 (Rev3)
  Sensor_prx = hc-sr04
  Servo = Basic Servo
  Reloj = Generic shrouded header - 10 pins [form="♂ (shrouded male)" package=THT]

nets:
  GND: Componente1.GND, Sensor_prx.GND, Servo.gnd, Reloj.GND
  VCC: Componente1.5V, Sensor_prx.VCC, Servo.vcc, Reloj.VCC
  N1: Componente1.D2_PWM, Sensor_prx.Trig
  N2: Componente1.D3_PWM, Sensor_prx.Echo
  N3: Componente1.D36, Reloj.CLK
  N4: Componente1.D38, Reloj.DAT
  N5: Componente1.D40, Reloj.RST
  N6: Componente1.D46, Servo.pulse

notes:
  Este es el modulo reloj que necesita 5 pins

custom parts:
  Generic shrouded header - 10 pins: Generic shrouded header
